# Fritzing sketch FritzingSchema (saved by Fritzing 0.9.3b)
breadboards: 1

parts:
  IC2 = Lopy [chip_label=IC]
  U3 = TMP36 [package=to-92]
  R1 = PHOTOCELL [package=photocell]
  R2 = Resistor [tolerance=±5% resistance=10k package=THT]

nets:
  N1: IC2.connector1, U3.GND, R2.Pin_1
  N2: IC2.connector2, U3.VCC, R1.P$2
  N3: IC2.connector10, U3.VOUT
  N4: IC2.connector13, R1.P$1, R2.Pin_0
